// Logisim project processor.circ as structural Verilog: 3 circuits, main circuit RegFile
module RegFile (
  input  [15:0] WriteDATA,
  input  [2:0] Read_Reg1_Index,
  input  [2:0] WriteINDEX,
  input  Reg_Write_Enable,
  input  [2:0] Read_Reg2_Index,
  input  Clock,
  output [15:0] Read_Data_1,
  output [15:0] Read_Data_2
);

  wire and_1_out, and_2_out, and_3_out, and_4_out, and_5_out, and_6_out, and_7_out, and_8_out,
       decoder_1_out0, decoder_1_out1, decoder_1_out2, decoder_1_out3, decoder_1_out4, decoder_1_out5,
       decoder_1_out6, decoder_1_out7;
  wire [15:0] r1_q, r2_q, r3_q, r4_q, r5_q, r6_q, r7_q, r8_q;

  Decoder #(.select(3)) decoder_1 (
    .out0(decoder_1_out0), .out1(decoder_1_out1), .out2(decoder_1_out2), .out3(decoder_1_out3),
    .out4(decoder_1_out4), .out5(decoder_1_out5), .out6(decoder_1_out6), .out7(decoder_1_out7),
    .sel(WriteINDEX));  // open: en
  and and_1 (and_1_out, decoder_1_out0, Reg_Write_Enable);
  and and_2 (and_2_out, decoder_1_out1, Reg_Write_Enable);
  and and_3 (and_3_out, decoder_1_out2, Reg_Write_Enable);
  and and_4 (and_4_out, decoder_1_out3, Reg_Write_Enable);
  and and_5 (and_5_out, decoder_1_out4, Reg_Write_Enable);
  and and_6 (and_6_out, decoder_1_out5, Reg_Write_Enable);
  and and_7 (and_7_out, decoder_1_out6, Reg_Write_Enable);
  and and_8 (and_8_out, decoder_1_out7, Reg_Write_Enable);
  Register #(.width(16)) r1 (.D(WriteDATA), .en(and_1_out), .Q(r1_q), .clk(Clock));  // open: clr
  Register #(.width(16)) r2 (.D(WriteDATA), .en(and_2_out), .Q(r2_q), .clk(Clock));  // open: clr
  Register #(.width(16)) r3 (.D(WriteDATA), .en(and_3_out), .Q(r3_q), .clk(Clock));  // open: clr
  Register #(.width(16)) r4 (.D(WriteDATA), .en(and_4_out), .Q(r4_q), .clk(Clock));  // open: clr
  Register #(.width(16)) r5 (.D(WriteDATA), .en(and_5_out), .Q(r5_q), .clk(Clock));  // open: clr
  Register #(.width(16)) r6 (.D(WriteDATA), .en(and_6_out), .Q(r6_q), .clk(Clock));  // open: clr
  Register #(.width(16)) r7 (.D(WriteDATA), .en(and_7_out), .Q(r7_q), .clk(Clock));  // open: clr
  Register #(.width(16)) r8 (.D(WriteDATA), .en(and_8_out), .Q(r8_q), .clk(Clock));  // open: clr
  Multiplexer #(.select(3), .width(16)) multiplexer_1 (
    .in0(r1_q), .in1(r2_q), .in2(r3_q), .in3(r4_q), .in4(r5_q), .in5(r6_q), .in6(r7_q), .in7(r8_q),
    .out(Read_Data_1), .sel(Read_Reg1_Index));  // open: en
  Multiplexer #(.select(3), .width(16)) multiplexer_2 (
    .in0(r1_q), .in1(r2_q), .in2(r3_q), .in3(r4_q), .in4(r5_q), .in5(r6_q), .in6(r7_q), .in7(r8_q),
    .out(Read_Data_2), .sel(Read_Reg2_Index));  // open: en
endmodule

module ALU (
  input  [15:0] input_A,
  input  [15:0] input_B,
  input  [2:0] Select,
  output [15:0] Result,
  output Equal,
  output Less
);

  wire [15:0] adder_1_out, and_1_out, or_1_out;

  Adder #(.width(16)) adder_1 (.a(input_A), .b(input_B), .out(adder_1_out));  // open: cin, cout
  assign and_1_out = input_A & input_B;  // AND_Gate and_1, 16 bits wide
  assign or_1_out = input_B | input_A;  // OR_Gate or_1, 16 bits wide
  Comparator #(.width(16)) comparator_1 (.a(input_A), .b(input_B), .eq(Equal), .lt(Less));  // open: gt
  Multiplexer #(.select(3), .width(16)) multiplexer_1 (
    .in0(adder_1_out), .in1(and_1_out), .in2(or_1_out), .in3(input_B), .in4(input_A), .out(Result),
    .sel(Select));  // open: in5, in6, in7, en

  // Other names for the same wires on the sheet: A[15:0] = input_A; B[15:0] = input_B; E = Equal; Les = Less;
  //   R[15:0] = Result; S[2:0] = Select
endmodule

module main (
);

  wire ALU_Equal, ALU_Less, ALUSrc, and_1_out, and_2_out, BLE, BNE, clock_1_out, Halt, Is_Rtn, Jump, MemRead,
       MemToReg, MemWrite, not_1_out, not_2_out, or_2_out, or_3_out, PC_Src, RaWrite, Reg_Write;
  wire [2:0] ALU_Op, rom_1_data_2;
  wire [5:0] bit_extender_1_out, multiplexer_4_out;
  wire [15:0] adder_1_out, alu_1_result, and_3_out, bit_extender_2_out, bit_extender_3_out, Branch_Target,
       multiplexer_1_out, multiplexer_2_out, multiplexer_3_out, multiplexer_5_out, multiplexer_6_out, PC_q,
       ra_q, ram_1_data, regfile_1_read_data_1, regfile_1_read_data_2, rom_1_data;
  wire [15:14] rom_2_data;

  Clock clock_1 (.out(clock_1_out));
  Multiplexer #(.width(16), .enable("false")) multiplexer_1 (
    .in0(multiplexer_3_out), .in1(Branch_Target), .out(multiplexer_1_out), .sel(PC_Src));
  Register #(.width(16)) ra (.D(adder_1_out), .en(RaWrite), .Q(ra_q), .clk(clock_1_out));  // open: clr
  Multiplexer #(.width(16), .enable("false")) multiplexer_2 (
    .in0(multiplexer_1_out), .in1(ra_q), .out(multiplexer_2_out), .sel(Is_Rtn));
  not not_1 (not_1_out, Halt);
  not not_2 (not_2_out, ALU_Equal);
  and and_1 (and_1_out, BNE, not_2_out);
  or or_1 (PC_Src, Jump, and_1_out, and_2_out);
  Register #(.width(16)) PC (.D(multiplexer_2_out), .en(not_1_out), .Q(PC_q), .clk(clock_1_out));  // open: clr
  or or_2 (or_2_out, ALU_Equal, ALU_Less);
  and and_2 (and_2_out, BLE, or_2_out);
  Adder #(.width(16)) adder_1 (.a(PC_q), .b(16'h1), .out(adder_1_out));  // open: cin, cout
  ROM #(.addrWidth(16), .dataWidth(16)) rom_1 (
    .addr(PC_q), .data({rom_1_data[15:12], rom_1_data_2, rom_1_data[8:0]}));  // open: sel
  Multiplexer #(.select(2), .width(16)) multiplexer_3 (
    .in0(adder_1_out), .out(multiplexer_3_out), .sel(2'b00), .en(1'b1));  // open: in1, in2, in3
  Adder #(.width(16)) adder_2 (.a(PC_q), .b(bit_extender_2_out), .out(Branch_Target));  // open: cin, cout
  Multiplexer #(.width(6), .enable("false")) multiplexer_4 (
    .in0({rom_1_data_2, rom_1_data[2:0]}), .in1(bit_extender_1_out), .out(multiplexer_4_out), .sel(or_3_out));
  assign bit_extender_1_out = {{3{rom_1_data[2]}}, rom_1_data[2:0]};  // Bit_Extender bit_extender_1
  or or_3 (or_3_out, BLE, BNE);
  assign bit_extender_2_out = {{10{multiplexer_4_out[5]}}, multiplexer_4_out};  // Bit_Extender bit_extender_2
  ROM #(.addrWidth(4), .dataWidth(16)) rom_2 (
    .addr(rom_1_data[15:12]),
    .data({rom_2_data, Halt, Is_Rtn, RaWrite, BNE, BLE, Jump, ALU_Op, MemToReg, MemWrite, MemRead, ALUSrc, Reg_Write}));  // open: sel
  RegFile regfile_1 (
    .WriteDATA(multiplexer_5_out), .Reg_Write_Enable(Reg_Write), .Clock(clock_1_out),
    .WriteINDEX(rom_1_data[5:3]), .Read_Data_1(regfile_1_read_data_1), .Read_Reg1_Index(rom_1_data[8:6]),
    .Read_Data_2(regfile_1_read_data_2), .Read_Reg2_Index(rom_1_data_2));
  assign bit_extender_3_out = {{15{1'b1}}, MemWrite};  // Bit_Extender bit_extender_3
  Multiplexer #(.width(16), .enable("false")) multiplexer_5 (
    .in0(alu_1_result), .in1(ram_1_data), .out(multiplexer_5_out), .sel(MemToReg));
  Multiplexer #(.width(16), .enable("false")) multiplexer_6 (
    .in0(regfile_1_read_data_2), .in1(bit_extender_2_out), .out(multiplexer_6_out), .sel(ALUSrc));
  assign and_3_out = regfile_1_read_data_2 & bit_extender_3_out;  // AND_Gate and_3, 16 bits wide
  ALU alu_1 (
    .input_A(regfile_1_read_data_1), .input_B(multiplexer_6_out), .Select(ALU_Op), .Result(alu_1_result),
    .Equal(ALU_Equal), .Less(ALU_Less));
  RAM #(.addrWidth(16), .dataWidth(16), .bus("separate")) ram_1 (
    .addr(alu_1_result), .din(and_3_out), .data(ram_1_data), .str(MemWrite), .sel(1'b1), .clk(clock_1_out),
    .ld(MemRead));  // open: clr

  // Notes on the sheet:
  //   Instr_Mem
  //   contents of rom_1 (hex, n*v repeats v):
  //   9001 900a 9212 208 a447 f000
  //   Control Unit
  //   Don't change the content of this:
  //   Immediate Generater
  //   contents of rom_2 (hex, n*v repeats v):
  //   1 21 41 3 23 43 95 88 81 63 200 400 100 900 1000 2000
  //   0001 0021 0041 0003 0023 0043 0095 0088
  //   0081 0063 0200 0400 0100 0900 1000 2000
  //   Data_Mem
endmodule
